# Fritzing sketch Schaltplan (saved by Fritzing 0.9.9b)
breadboards: 1

parts:
  Gizwits_WiFi_Witty_ESP-12F1 = Gizwits WiFi Witty ESP-12F
  DHT1 = DHT22 Humidity and Temperature Sensor
  U2 = V_REG_LD1117VXX [package=78xxl]
  RFID1 = RFID RC522 Module [package=THT]
  U3 = V_REG_LD1117VXX [package=78xxl]

nets:
  N1: Gizwits_WiFi_Witty_ESP-12F1.GPIO14, DHT1.DATA, RFID1.SCK
  N2: Gizwits_WiFi_Witty_ESP-12F1.GPIO12, RFID1.MISO
  N3: Gizwits_WiFi_Witty_ESP-12F1.GPIO13, RFID1.MOSI
  N4: Gizwits_WiFi_Witty_ESP-12F1.VCC, U2.IN, U3.IN
  GND: Gizwits_WiFi_Witty_ESP-12F1.GND, DHT1.GND, U2.GND, RFID1.GND, U3.GND
  N5: Gizwits_WiFi_Witty_ESP-12F1.GPIO5, RFID1.NSS
  N6: Gizwits_WiFi_Witty_ESP-12F1.RXD, RFID1.RST
  N7: DHT1.VDD, U2.OUT
  N8: RFID1.VCC, U3.OUT

custom parts:
  RFID RC522 Module: The RC522 is a 13.56MHz RFID module that is based on the MFRC522 controller from NXP semiconductors. The module can supports I2C, SPI and UART and normally is shipped with a RFID card and key fob. It is commonly used in attendance systems and other person/object identification applications.
